// Logisim project robertson final 4 bit_2.circ as structural Verilog: 1 circuit, main circuit main
module main (
  input  COUNTER,
  input  in_2,
  input  in_3,
  input  [3:0] MULTIPLICAND,
  input  [3:0] MULTIPLIER,
  input  PRODUCT,
  input  in_7
);

  wire and_2_out, and_3_out, and_4_out, and_5_out, and_6_out, and_7_out, clock_1_out, d_ff_1_q, nand_1_out,
       not_2_out, not_3_out, not_5_out, not_6_out, not_7_out, not_8_out, or_2_out, RESET_out,
       shift_register_1_out, t_ff_1_q, xnor_1_out;
  wire [3:0] adder_1_out, and_1_out, not_1_out, not_4_out, shift_register_1_q3, shift_register_2_q3,
       xor_1_out;
  wire [3:3] or_1_out, shift_register_2_out;
  wire [4:0] counter_1_q;

  Button RESET (.out(RESET_out));
  _7_Segment_Display u_7_segment_display_1 (
    .f(not_1_out[2]), .a(not_1_out[2]), .b(in_7), .e(not_1_out[2]), .d(not_1_out[2]), .c(in_7));  // open: g, dp
  _7_Segment_Display u_7_segment_display_2 (
    .f(xnor_1_out), .a(xnor_1_out), .b(in_7), .e(xnor_1_out), .d(xnor_1_out), .c(in_7));  // open: g, dp
  assign and_1_out = {4{shift_register_2_out[3]}} & MULTIPLICAND;  // AND_Gate and_1, 4 bits wide
  assign xor_1_out = and_1_out ^ {4{or_1_out[3]}};  // XOR_Gate xor_1, 4 bits wide
  T_Flip_Flop #(.trigger("falling")) t_ff_1 (
    .clk(and_3_out), .T(in_3), .Q(t_ff_1_q), .reset(RESET_out), .en(in_3));  // open: Qn, preset
  assign not_1_out = ~shift_register_1_q3;  // NOT_Gate not_1, 4 bits wide
  _7_Segment_Display u_7_segment_display_3 (
    .f(not_1_out[0]), .a(not_1_out[0]), .b(in_7), .e(not_1_out[0]), .d(not_1_out[0]), .c(in_7));  // open: g, dp
  _7_Segment_Display u_7_segment_display_4 (
    .f(not_1_out[1]), .a(not_1_out[1]), .b(in_7), .e(not_1_out[1]), .d(not_1_out[1]), .c(in_7));  // open: g, dp
  Adder #(.width(4)) adder_1 (
    .a(xor_1_out), .b(shift_register_1_q3), .out(adder_1_out), .cin(or_1_out[3]));  // open: cout
  and and_2 (and_2_out, t_ff_1_q, not_3_out);
  _7_Segment_Display u_7_segment_display_5 (
    .f(not_4_out[3]), .a(not_4_out[3]), .b(in_7), .e(not_4_out[3]), .d(not_4_out[3]), .c(in_7));  // open: g, dp
  Shift_Register #(.length(4)) shift_register_1 (
    .shift(and_2_out), .in(d_ff_1_q), .clk(and_3_out), .out(shift_register_1_out), .load(not_2_out),
    .clr(RESET_out), .d0(adder_1_out[3]), .q0(shift_register_1_q3[3]), .d1(adder_1_out[2]),
    .q1(shift_register_1_q3[2]), .d2(adder_1_out[1]), .q2(shift_register_1_q3[1]), .d3(adder_1_out[0]),
    .q3(shift_register_1_q3[0]));
  not not_2 (not_2_out, and_2_out);
  not not_3 (not_3_out, and_4_out);
  assign not_4_out = ~shift_register_2_q3;  // NOT_Gate not_4, 4 bits wide
  _7_Segment_Display u_7_segment_display_6 (
    .f(not_4_out[1]), .a(not_4_out[1]), .b(in_7), .e(not_4_out[1]), .d(not_4_out[1]), .c(in_7));  // open: g, dp
  _7_Segment_Display u_7_segment_display_7 (
    .f(not_4_out[2]), .a(not_4_out[2]), .b(in_7), .e(not_4_out[2]), .d(not_4_out[2]), .c(in_7));  // open: g, dp
  Shift_Register #(.length(4)) shift_register_2 (
    .shift(and_2_out), .in(shift_register_1_out), .clk(and_3_out), .out(shift_register_2_out[3]),
    .load(and_4_out), .clr(RESET_out), .d0(MULTIPLIER[3]), .q0(shift_register_2_q3[3]), .d1(MULTIPLIER[2]),
    .q1(shift_register_2_q3[2]), .d2(MULTIPLIER[1]), .q2(shift_register_2_q3[1]), .d3(MULTIPLIER[0]),
    .q3(shift_register_2_q3[0]));
  and and_3 (and_3_out, clock_1_out, PRODUCT, nand_1_out);
  _7_Segment_Display u_7_segment_display_8 (
    .f(not_4_out[0]), .a(not_4_out[0]), .b(in_7), .e(not_4_out[0]), .d(not_4_out[0]), .c(in_7));  // open: g, dp
  Counter #(.width(5), .max('h1f)) counter_1 (
    .load(COUNTER), .count(in_2), .Q(counter_1_q), .clk(and_3_out), .clr(RESET_out));  // open: D, carry
  not not_5 (not_5_out, counter_1_q[4]);
  not not_6 (not_6_out, counter_1_q[1]);
  and and_4 (and_4_out, not_5_out, counter_1_q[0], not_6_out, not_8_out, not_7_out);
  or or_1 (or_1_out[3], and_6_out, and_7_out);
  Clock clock_1 (.out(clock_1_out));
  and and_5 (and_5_out, MULTIPLICAND[3], shift_register_2_out[3]);
  not not_7 (not_7_out, counter_1_q[3]);
  not not_8 (not_8_out, counter_1_q[2]);
  and and_6 (and_6_out, counter_1_q[3], counter_1_q[0]);
  D_Flip_Flop d_ff_1 (.clk(and_3_out), .D(or_2_out), .Q(d_ff_1_q), .reset(RESET_out));  // open: Qn, preset, en
  or or_2 (or_2_out, and_5_out, d_ff_1_q);
  and and_7 (and_7_out, counter_1_q[3], shift_register_2_out[3]);
  nand nand_1 (nand_1_out, counter_1_q[3], counter_1_q[1]);
  xnor xnor_1 (xnor_1_out, MULTIPLICAND[3], MULTIPLIER[3]);

  // Notes on the sheet:
  //   X
  //   ADDER
  //   ACC
  //   ROBERTSON'S TWO'S COMPLEMENT MULTIPLIER (4 BIT)
  //   Q
  //   CLOCK ENABLE
  //   BY:
  //    CHAITHANYA .B.S
  //   ROLL NO: 11CO27
  //   III SEM B.TECH
  //   F(SIGN LOGIC)
endmodule
