// Logisim project robertson_3.circ as structural Verilog: 1 circuit, main circuit main
module main (
  input  [3:0] in_1,
  input  [3:0] in_2,
  input  in_3,
  input  in_4,
  input  in_5,
  input  in_6
);

  wire adder_1_cout, and_2_out, and_3_out, and_4_out, and_5_out, clear_out, clock_1_out, d_ff_1_q,
       nand_1_out, not_1_out, not_2_out, not_3_out, not_4_out, not_5_out, not_6_out, or_1_out,
       shift_register_1_out, t_ff_1_q;
  wire [3:0] adder_1_out, and_1_out, shift_register_1_q3, xor_1_out;
  wire [3:3] and_6_out, shift_register_2_out;
  wire [4:0] counter_1_q;

  assign and_1_out = {4{shift_register_2_out[3]}} & in_2;  // AND_Gate and_1, 4 bits wide
  assign xor_1_out = and_1_out ^ {4{and_6_out[3]}};  // XOR_Gate xor_1, 4 bits wide
  T_Flip_Flop #(.trigger("falling")) t_ff_1 (
    .clk(and_3_out), .T(in_6), .Q(t_ff_1_q), .reset(clear_out), .en(in_6));  // open: Qn, preset
  Adder #(.width(4)) adder_1 (
    .a(xor_1_out), .b(shift_register_1_q3), .out(adder_1_out), .cin(and_6_out[3]), .cout(adder_1_cout));
  Shift_Register #(.length(4)) shift_register_1 (
    .shift(and_2_out), .in(d_ff_1_q), .clk(and_3_out), .out(shift_register_1_out), .load(not_1_out),
    .clr(clear_out), .d0(adder_1_out[3]), .q0(shift_register_1_q3[3]), .d1(adder_1_out[2]),
    .q1(shift_register_1_q3[2]), .d2(adder_1_out[1]), .q2(shift_register_1_q3[1]), .d3(adder_1_out[0]),
    .q3(shift_register_1_q3[0]));
  not not_1 (not_1_out, and_2_out);
  and and_2 (and_2_out, t_ff_1_q, not_2_out);
  Shift_Register #(.length(4)) shift_register_2 (
    .shift(and_2_out), .in(shift_register_1_out), .clk(and_3_out), .out(shift_register_2_out[3]),
    .load(and_5_out), .clr(clear_out), .d0(in_1[3]), .d1(in_1[2]), .d2(in_1[1]), .d3(in_1[0]));  // open: q0, q1, q2, q3
  not not_2 (not_2_out, and_5_out);
  Counter #(.width(5), .max('h1f)) counter_1 (
    .load(in_4), .count(in_5), .Q(counter_1_q), .clk(and_3_out), .clr(clear_out));  // open: D, carry
  and and_3 (and_3_out, clock_1_out, in_3, nand_1_out);
  Clock clock_1 (.out(clock_1_out));
  and and_4 (and_4_out, in_2[3], shift_register_2_out[3]);
  not not_3 (not_3_out, counter_1_q[4]);
  not not_4 (not_4_out, counter_1_q[2]);
  not not_5 (not_5_out, counter_1_q[3]);
  not not_6 (not_6_out, counter_1_q[1]);
  and and_5 (and_5_out, not_3_out, counter_1_q[0], not_6_out, not_4_out, not_5_out);
  or or_1 (or_1_out, and_4_out, d_ff_1_q);
  D_Flip_Flop d_ff_1 (.clk(and_3_out), .D(or_1_out), .Q(d_ff_1_q), .reset(clear_out));  // open: Qn, preset, en
  and and_6 (and_6_out[3], counter_1_q[3], shift_register_2_out[3]);
  Button clear (.out(clear_out));
  nand nand_1 (nand_1_out, counter_1_q[3], counter_1_q[1]);
endmodule
