// Logisim project robertson_8bit.circ as structural Verilog: 1 circuit, main circuit main
module main (
  input  [7:0] in_1,
  input  [7:0] in_2,
  input  in_3,
  input  in_4,
  input  in_5,
  input  in_6
);

  wire adder_1_cout, and_2_out, and_3_out, and_4_out, and_5_out, clear_out, clock_1_out, d_ff_1_q,
       nand_1_out, not_1_out, not_2_out, not_3_out, not_4_out, not_5_out, not_6_out, or_1_out,
       shift_register_1_out, t_ff_1_q;
  wire [4:0] counter_1_q;
  wire [7:0] adder_1_out, and_1_out, shift_register_1_q7, xor_1_out;
  wire [7:7] and_6_out, shift_register_2_q7;

  assign and_1_out = {8{shift_register_2_q7[7]}} & in_1;  // AND_Gate and_1, 8 bits wide
  assign xor_1_out = and_1_out ^ {8{and_6_out[7]}};  // XOR_Gate xor_1, 8 bits wide
  T_Flip_Flop #(.trigger("falling")) t_ff_1 (
    .clk(and_3_out), .T(in_6), .Q(t_ff_1_q), .reset(clear_out), .en(in_6));  // open: Qn, preset
  Adder adder_1 (.a(xor_1_out), .b(shift_register_1_q7), .out(adder_1_out), .cin(and_6_out[7]), .cout(adder_1_cout));
  Shift_Register shift_register_1 (
    .shift(and_2_out), .in(d_ff_1_q), .clk(and_3_out), .out(shift_register_1_out), .load(not_1_out),
    .clr(clear_out), .d0(adder_1_out[7]), .q0(shift_register_1_q7[7]), .d1(adder_1_out[6]),
    .q1(shift_register_1_q7[6]), .d2(adder_1_out[5]), .q2(shift_register_1_q7[5]), .d3(adder_1_out[4]),
    .q3(shift_register_1_q7[4]), .d4(adder_1_out[3]), .q4(shift_register_1_q7[3]), .d5(adder_1_out[2]),
    .q5(shift_register_1_q7[2]), .d6(adder_1_out[1]), .q6(shift_register_1_q7[1]), .d7(adder_1_out[0]),
    .q7(shift_register_1_q7[0]));
  not not_1 (not_1_out, and_2_out);
  and and_2 (and_2_out, t_ff_1_q, not_2_out);
  not not_2 (not_2_out, and_5_out);
  Shift_Register shift_register_2 (
    .shift(and_2_out), .in(shift_register_1_out), .clk(and_3_out), .load(and_5_out), .clr(clear_out),
    .d0(in_2[7]), .d1(in_2[6]), .d2(in_2[5]), .d3(in_2[4]), .d4(in_2[3]), .d5(in_2[2]), .d6(in_2[1]),
    .d7(in_2[0]), .q7(shift_register_2_q7[7]));  // open: out, q0, q1, q2, q3, q4, q5, q6
  Counter #(.width(5), .max('h1f)) counter_1 (
    .load(in_4), .count(in_5), .Q(counter_1_q), .clk(and_3_out), .clr(clear_out));  // open: D, carry
  and and_3 (and_3_out, clock_1_out, in_3, nand_1_out);
  Clock clock_1 (.out(clock_1_out));
  and and_4 (and_4_out, in_1[7], shift_register_2_q7[7]);
  not not_3 (not_3_out, counter_1_q[3]);
  not not_4 (not_4_out, counter_1_q[1]);
  not not_5 (not_5_out, counter_1_q[4]);
  not not_6 (not_6_out, counter_1_q[2]);
  and and_5 (and_5_out, not_5_out, counter_1_q[0], not_4_out, not_6_out, not_3_out);
  or or_1 (or_1_out, and_4_out, d_ff_1_q);
  D_Flip_Flop d_ff_1 (.clk(and_3_out), .D(or_1_out), .Q(d_ff_1_q), .reset(clear_out));  // open: Qn, preset, en
  and and_6 (and_6_out[7], counter_1_q[4], shift_register_2_q7[7]);
  Button clear (.out(clear_out));
  nand nand_1 (nand_1_out, counter_1_q[4], counter_1_q[0]);
endmodule
